// Logisim project LAB-2,ANS-1.circ as structural Verilog: 1 circuit, main circuit main
module main (
  input  in_1,
  input  in_2,
  input  in_3,
  input  in_4,
  input  in_5,
  input  in_6,
  input  in_7,
  input  in_8,
  input  in_9,
  input  in_10,
  input  in_11,
  input  in_12,
  input  in_13,
  input  in_14,
  input  in_15,
  input  in_16,
  input  in_17,
  input  in_18,
  input  in_19,
  input  in_20,
  output out_21,
  output out_22,
  output out_23,
  output out_24,
  output out_25,
  output out_26,
  output out_27,
  output out_28,
  output out_29,
  output out_30
);

  wire nand_1_out, nand_3_out, nand_4_out, nand_5_out, nand_6_out, nand_7_out, nand_8_out, nand_9_out,
       nand_13_out;

  nand nand_1 (nand_1_out, in_17, in_20);
  nand nand_2 (out_21, in_1, in_1);
  nand nand_3 (nand_3_out, in_3, in_5);
  nand nand_4 (nand_4_out, in_7, in_7);
  nand nand_5 (nand_5_out, in_10, in_10);
  nand nand_6 (nand_6_out, in_11, in_12);
  nand nand_7 (nand_7_out, in_14, in_16);
  nand nand_8 (nand_8_out, in_17, nand_1_out);
  nand nand_9 (nand_9_out, nand_1_out, in_20);
  nand nand_10 (out_23, nand_3_out, nand_3_out);
  nand nand_11 (out_25, nand_4_out, nand_5_out);
  nand nand_12 (out_27, nand_6_out, nand_7_out);
  nand nand_13 (nand_13_out, nand_8_out, nand_9_out);
  nand nand_14 (out_29, nand_13_out, nand_13_out);
  not not_1 (out_22, in_2);
  and and_1 (out_24, in_4, in_6);
  or or_1 (out_26, in_8, in_9);
  xor xor_1 (out_28, in_13, in_15);
  xnor xnor_1 (out_30, in_18, in_19);

  // Notes on the sheet:
  //   NOT gate using NAND gate
  //   AND gate using NAND gate
  //   OR gate using NAND gate
  //                                     XOR gate using NAND gate
  //                                          XNOR gate only NAND gate
endmodule
